# Fritzing sketch receiver (saved by Fritzing 0.9.1b)

parts:
  Part1 = Arduino Uno (Rev3)
  Grove1 = Grove 4 Digit Display
  D1 = LED_BARGRAPH_10 [package=led_bargaph_10]  # not connected
  Grove2 = Grove 4 Digit Display

nets:
  N1: Part1.A4/SDA, Grove2.CLK
  N2: Part1.A5/SCL, Grove2.DIO
  N3: Part1.D8, Grove1.DIO
  N4: Part1.D7, Grove1.CLK
  3V3: Part1.3V3, Grove1.VCC
  5V: Part1.5V, Grove2.VCC
  GND: Part1.GND, Grove1.GND, Grove2.GND
