# Fritzing sketch sketch (saved by Fritzing 0.9.1b)
breadboards: 1

parts:
  Part1 = Arduino Uno (Rev3)
  Part2 = Breakout Board for Electret Microphone
  LED1 = LED - 5mm [color="Red (633nm)" package="5 mm [THT]"]
  LED2 = LED - 5mm [color="Yellow (595nm)" package="5 mm [THT]"]
  R1 = Resistor [tolerance=±5% resistance=220 package=THT]
  R2 = Resistor [tolerance=±5% resistance=220 package=THT]
  R3 = Resistor [tolerance=±5% resistance=220 package=THT]
  LED3 = smd LED [color="Green (555nm)" package="0603 [SMD]"]

nets:
  N1: Part1.A0, Part2.AUD
  GND: Part1.GND, Part2.GND, LED1.cathode, LED2.cathode, LED3.cathode
  N2: Part1.D3_PWM, R3.Pin_1
  N3: Part1.D5_PWM, R2.Pin_1
  N4: Part1.D6_PWM, R1.Pin_1
  3V3: Part1.3V3, Part2.VCC
  N5: LED1.anode, R3.Pin_0
  N6: LED2.anode, R2.Pin_0
  N7: R1.Pin_0, LED3.anode
